# Fritzing sketch chenillard (saved by Fritzing 0.9.3b)
breadboards: 1

parts:
  Composant1 = Arduino Uno (Rev3)
  LED1 = LED - 5mm [color="Green (565nm)" package="5 mm [THT]"]
  LED2 = LED - 5mm [color="Orange (620nm)" package="5 mm [THT]"]
  LED3 = LED - 5mm [color="Red (633nm)" package="5 mm [THT]"]

nets:
  N1: Composant1.GND, LED1.cathode, LED2.cathode, LED3.cathode
  N2: Composant1.D4, LED1.anode
  N3: Composant1.D5_PWM, LED2.anode
  N4: Composant1.D6_PWM, LED3.anode

// code stored in the sketch: chenillard.ino
#define PIN_GREEN 4
#define PIN_YELLOW 5
#define PIN_RED 6
// the setup function runs once when you press reset or power the board
void setup() {
  // initialize digital pin LED_BUILTIN as an output.
  pinMode(PIN_GREEN, OUTPUT);
  pinMode(PIN_YELLOW, OUTPUT);
  pinMode(PIN_RED, OUTPUT);
}


// the loop function runs over and over again forever
void loop() {
  digitalWrite(PIN_GREEN, HIGH);
  digitalWrite(PIN_RED, LOW);
  delay(1000);
  
  digitalWrite(PIN_YELLOW, HIGH);
  digitalWrite(PIN_GREEN, LOW);
  delay(1000);


  
  digitalWrite(PIN_RED, HIGH);
  digitalWrite(PIN_YELLOW, LOW);
  delay(1000);
}
