# Fritzing sketch voltmetre_lcd (saved by Fritzing 0.9.3b)
circuit board: 6.88566cm x 5.36311cm
breadboards: 2

parts:
  LCD1 = LCD screen
  R2 = Resistor [tolerance=±5% resistance=220 package=THT]
  Contrast1 = Rotary Potentiometer (Small) [maximum_resistance=100kΩ package=THT]
  Arduino1 = Arduino Uno (Rev3)
  R5 = Resistor [tolerance=±5% resistance=1k package=THT]
  R6 = Resistor [tolerance=±5% resistance=1k package=THT]  # not connected
  R7 = Resistor [tolerance=±5% resistance=470 package=THT]

nets:
  VSS: LCD1.VSS, LCD1.R/W, LCD1.LED-, Contrast1.leg1, Arduino1.GND, R7.Pin_1
  VDD: LCD1.VDD, R2.Pin_1, Contrast1.leg2, Arduino1.5V
  N1: LCD1.V0, Contrast1.wiper
  N2: LCD1.RS, Arduino1.D12/MISO
  N3: LCD1.E, Arduino1.D11_PWM/MOSI
  N4: LCD1.DB4, Arduino1.D5_PWM
  N5: LCD1.DB5, Arduino1.D4
  N6: LCD1.DB6, Arduino1.D3_PWM
  N7: LCD1.DB7, Arduino1.D2
  N8: LCD1.LED+, R2.Pin_0
  N9: Arduino1.A0, R5.Pin_1, R7.Pin_0

notes:
  Code and more on character LCDs at http://arduino.cc/en/Tutorial/LiquidCrystal

// code stored in the sketch: voltmetre+lcd.ino
+#define R1 2000
#define R2 560
#define PIN_VOLTMETRE A0

#define MAX_VOLTS_INPUT 22.857F
#define RATION_VOLT (float)(22.857F / 5.0F)
#define RATIO_ADC (float)(5.0F / 1024.0F)
float calculateVin(uint16_t vADC) {
  return  RATIO_ADC * (float) vADC * RATION_VOLT;
}


void setup() {
  // put your setup code here, to run once:
  Serial.begin(9600);
}

void loop() {
  // put your main code here, to run repeatedly:
  Serial.print("Valeur lue : ");
  Serial.println(calculateVin(analogRead(PIN_VOLTMETRE)));
  delay(900);
}

// code stored in the sketch: voltmetre.ino
#define R1 2000
#define R2 560
#define PIN_VOLTMETRE A0

#define MAX_VOLTS_INPUT 22.857F
#define RATION_VOLT (float)(22.857F / 5.0F)
#define RATIO_ADC (float)(5.0F / 1024.0F)
float calculateVin(uint16_t vADC) {
  return  RATIO_ADC * (float) vADC * RATION_VOLT;
}


void setup() {
  // put your setup code here, to run once:
  Serial.begin(9600);
}

void loop() {
  // put your main code here, to run repeatedly:
  Serial.print("Valeur lue : ");
  Serial.println(calculateVin(analogRead(PIN_VOLTMETRE)));
  delay(900);
}

// code stored in the sketch: voltmetre_lcd.ino
#define R1 2000
#define R2 560
#define PIN_VOLTMETRE A0

#define MAX_VOLTS_INPUT 22.857F
#define RATION_VOLT (float)(22.857F / 5.0F)
#define RATIO_ADC (float)(5.0F / 1024.0F)
float calculateVin(uint16_t vADC) {
  return  RATIO_ADC * (float) vADC * RATION_VOLT;
}


void setup() {
  // put your setup code here, to run once:
  Serial.begin(9600);
}

void loop() {
  // put your main code here, to run repeatedly:
  Serial.print("Valeur lue : ");
  Serial.println(calculateVin(analogRead(PIN_VOLTMETRE)));
  delay(900);
}
